# Fritzing sketch Perfboard-Attiny85-Fan-Control (saved by Fritzing 0.9.3b)
perfboards: 1

parts:
  U1 = attiny85 [package=dip]
  R1 = Resistor [tolerance=±5% resistance=2k package=THT]
  Rt = Temperature Sensor (Thermistor) [part_number="NTC 5K B3470" package=THT]
  LED1 = smd LED [color="Red (633nm)" package="1206 [SMD]"]
  R4 = Resistor [tolerance=±5% resistance=220 package=THT]
  Power_plug = Power plug [part_number=5V]
  Q1 = Basic FET N-Channel [part_number=IRL3103 package="DPak [SMD]"]
  Fan_Motor = DC Motor
  D1 = Rectifier Diode [part_number=SR360 package="300 mil [THT]"]

nets:
  N1: U1.Pin_3, R4.Pin_1
  N2: U1.Pin_4, R1.Pin_1, LED1.cathode, Power_plug.GND, Q1.source
  N3: U1.Pin_6, Q1.Gate
  N4: U1.Pin_7, R1.Pin_0, Rt.pin_1
  N5: U1.Pin_8, Rt.pin_0, Power_plug.VCC, Fan_Motor.pin_1, D1.cathode
  N6: LED1.anode, R4.Pin_0
  N7: Q1.drain, Fan_Motor.pin_2, D1.anode

custom parts:
  Temperature Sensor (Thermistor): A NTC Thermistor (Temperature Sensor)
